# Fritzing sketch Mood_lamp (saved by Fritzing 0.9.3b)

parts:
  U1 = WS2812 RGB LED strip
  WeMos_D1_R1 = WeMos D1 R2
  DHT2 = DHT11 Humitidy and Temperature Sensor (3 pins)

nets:
  GND: U1.GND, WeMos_D1_R1.GND, DHT2.Gnd
  VCC: U1.VCC, WeMos_D1_R1.5V, DHT2.Plus
  N1: U1.DIN, WeMos_D1_R1.D8
  N2: WeMos_D1_R1.(D6), DHT2.Signal

custom parts:
  WS2812 RGB LED strip: WS2812 strip
  WeMos D1 R2: The D1 R2 is a mini wifi board based on the ESP-8266EX.
  DHT11 Humitidy and Temperature Sensor (3 pins): DHT11 Humidity and Temperature Sensor (3 pins).
